# Fritzing sketch load_cell_sensor_modules_board (saved by Fritzing 0.9.3b)
circuit board: 14.3243cm x 7.11424cm
circuit board: 7.08176cm x 7.08771cm
breadboards: 1

parts:
  J23 = female pin header, 10 pins [form="♀ (female)"]
  J24 = female pin header, 4 pins [form="♀ (female)"]
  J25 = female pin header, 4 pins [form="♀ (female)"]
  J26 = female pin header, 4 pins [form="♀ (female)"]
  J28 = female pin header, 4 pins [form="♀ (female)"]
  J32 = female pin header, 10 pins [form="♀ (female)"]
  J33 = female pin header, 4 pins [form="♀ (female)"]
  J34 = female pin header, 4 pins [form="♀ (female)"]
  J35 = female pin header, 4 pins [form="♀ (female)"]
  J37 = female pin header, 4 pins [form="♀ (female)"]
  J130 = female pin header, 6 pins [form="♀ (female)"]  # not connected
  J131 = female pin header, 4 pins [form="♀ (female)"]
  J132 = female pin header, 6 pins [form="♀ (female)"]  # not connected
  J133 = female pin header, 6 pins [form="♀ (female)"]  # not connected
  J134 = female pin header, 4 pins [form="♀ (female)"]
  J135 = female pin header, 4 pins [form="♀ (female)"]
  J136 = female pin header, 10 pins [form="♀ (female)"]
  J137 = female pin header, 4 pins [form="♀ (female)"]
  J138 = female pin header, 6 pins [form="♀ (female)"]  # not connected
  J139 = female pin header, 6 pins [form="♀ (female)"]  # not connected
  J140 = female pin header, 4 pins [form="♀ (female)"]
  J141 = female pin header, 6 pins [form="♀ (female)"]  # not connected
  J142 = female pin header, 4 pins [form="♀ (female)"]
  J143 = female pin header, 4 pins [form="♀ (female)"]
  J144 = female pin header, 4 pins [form="♀ (female)"]
  J145 = female pin header, 10 pins [form="♀ (female)"]
  J146 = female pin header, 6 pins [form="♀ (female)"]  # not connected
  J147 = female pin header, 6 pins [form="♀ (female)"]  # not connected
  J148 = female pin header, 6 pins [form="♀ (female)"]  # not connected
  J149 = female pin header, 4 pins [form="♀ (female)"]
  J150 = female pin header, 6 pins [form="♀ (female)"]  # not connected
  J151 = female pin header, 6 pins [form="♀ (female)"]  # not connected
  J152 = female pin header, 4 pins [form="♀ (female)"]
  J153 = female pin header, 4 pins [form="♀ (female)"]
  J154 = female pin header, 10 pins [form="♀ (female)"]
  J155 = female pin header, 4 pins [form="♀ (female)"]
  J156 = female pin header, 6 pins [form="♀ (female)"]  # not connected
  J157 = female pin header, 6 pins [form="♀ (female)"]  # not connected
  J158 = female pin header, 4 pins [form="♀ (female)"]
  J159 = female pin header, 6 pins [form="♀ (female)"]  # not connected
  J160 = female pin header, 4 pins [form="♀ (female)"]
  J161 = female pin header, 4 pins [form="♀ (female)"]
  J162 = female pin header, 4 pins [form="♀ (female)"]
  J163 = female pin header, 10 pins [form="♀ (female)"]
  J164 = female pin header, 6 pins [form="♀ (female)"]  # not connected
  J165 = female pin header, 6 pins [form="♀ (female)"]  # not connected
  J167 = female pin header, 6 pins [form="♀ (female)"]  # not connected
  J168 = female pin header, 4 pins [form="♀ (female)"]
  J170 = female pin header, 6 pins [form="♀ (female)"]  # not connected
  J172 = female pin header, 6 pins [form="♀ (female)"]  # not connected
  J174 = female pin header, 4 pins [form="♀ (female)"]
  J177 = female pin header, 4 pins [form="♀ (female)"]
  J178 = female pin header, 10 pins [form="♀ (female)"]
  J181 = female pin header, 4 pins [form="♀ (female)"]
  J182 = female pin header, 6 pins [form="♀ (female)"]  # not connected
  J185 = female pin header, 6 pins [form="♀ (female)"]  # not connected
  J187 = female pin header, 4 pins [form="♀ (female)"]
  J188 = female pin header, 6 pins [form="♀ (female)"]  # not connected
  J190 = female pin header, 4 pins [form="♀ (female)"]
  J193 = female pin header, 4 pins [form="♀ (female)"]
  J195 = female pin header, 4 pins [form="♀ (female)"]
  J196 = female pin header, 10 pins [form="♀ (female)"]
  J198 = female pin header, 6 pins [form="♀ (female)"]  # not connected
  J201 = female pin header, 6 pins [form="♀ (female)"]  # not connected

nets:
  N1: J23.pin1, J25.pin2
  N2: J23.pin2, J25.pin3
  N3: J23.pin3, J24.pin2
  N4: J23.pin4, J24.pin3
  N5: J23.pin5, J28.pin2
  N6: J23.pin6, J28.pin3
  N7: J23.pin7, J26.pin2
  N8: J23.pin8, J26.pin3
  N9: J23.pin9, J24.pin1, J25.pin1, J26.pin1, J28.pin1
  N10: J23.pin10, J24.pin4, J25.pin4, J26.pin4, J28.pin4
  N11: J32.pin1, J34.pin2
  N12: J32.pin2, J34.pin3
  N13: J32.pin3, J33.pin2
  N14: J32.pin4, J33.pin3
  N15: J32.pin5, J37.pin2
  N16: J32.pin6, J37.pin3
  N17: J32.pin7, J35.pin2
  N18: J32.pin8, J35.pin3
  N19: J32.pin9, J33.pin1, J34.pin1, J35.pin1, J37.pin1
  N20: J32.pin10, J33.pin4, J34.pin4, J35.pin4, J37.pin4
  N21: J131.pin1, J134.pin1, J135.pin1, J136.pin9, J137.pin1, J140.pin1, J142.pin1, J143.pin1, J144.pin1, J145.pin9, J149.pin1, J152.pin1, J153.pin1, J154.pin9, J155.pin1, J158.pin1, J160.pin1, J161.pin1, J162.pin1, J163.pin9
  N22: J131.pin2, J136.pin7
  N23: J131.pin3, J136.pin8
  N24: J131.pin4, J134.pin4, J135.pin4, J136.pin10, J137.pin4, J140.pin4, J142.pin4, J143.pin4, J144.pin4, J145.pin10, J149.pin4, J152.pin4, J153.pin4, J154.pin10, J155.pin4, J158.pin4, J160.pin4, J161.pin4, J162.pin4, J163.pin10
  N25: J134.pin2, J136.pin3
  N26: J134.pin3, J136.pin4
  N27: J135.pin2, J136.pin5
  N28: J135.pin3, J136.pin6
  N29: J136.pin1, J137.pin2
  N30: J136.pin2, J137.pin3
  N31: J140.pin2, J145.pin5
  N32: J140.pin3, J145.pin6
  N33: J142.pin2, J145.pin7
  N34: J142.pin3, J145.pin8
  N35: J143.pin2, J145.pin1
  N36: J143.pin3, J145.pin2
  N37: J144.pin2, J145.pin3
  N38: J144.pin3, J145.pin4
  N39: J149.pin2, J154.pin7
  N40: J149.pin3, J154.pin8
  N41: J152.pin2, J154.pin3
  N42: J152.pin3, J154.pin4
  N43: J153.pin2, J154.pin5
  N44: J153.pin3, J154.pin6
  N45: J154.pin1, J155.pin2
  N46: J154.pin2, J155.pin3
  N47: J158.pin2, J163.pin5
  N48: J158.pin3, J163.pin6
  N49: J160.pin2, J163.pin7
  N50: J160.pin3, J163.pin8
  N51: J161.pin2, J163.pin1
  N52: J161.pin3, J163.pin2
  N53: J162.pin2, J163.pin3
  N54: J162.pin3, J163.pin4
  N55: J168.pin1, J174.pin1, J177.pin1, J178.pin9, J181.pin1, J187.pin1, J190.pin1, J193.pin1, J195.pin1, J196.pin9
  N56: J168.pin2, J178.pin7
  N57: J168.pin3, J178.pin8
  N58: J168.pin4, J174.pin4, J177.pin4, J178.pin10, J181.pin4, J187.pin4, J190.pin4, J193.pin4, J195.pin4, J196.pin10
  N59: J174.pin2, J178.pin3
  N60: J174.pin3, J178.pin4
  N61: J177.pin2, J178.pin5
  N62: J177.pin3, J178.pin6
  N63: J178.pin1, J181.pin2
  N64: J178.pin2, J181.pin3
  N65: J187.pin2, J196.pin5
  N66: J187.pin3, J196.pin6
  N67: J190.pin2, J196.pin7
  N68: J190.pin3, J196.pin8
  N69: J193.pin2, J196.pin1
  N70: J193.pin3, J196.pin2
  N71: J195.pin2, J196.pin3
  N72: J195.pin3, J196.pin4
