# Fritzing sketch initial_main_board (saved by Fritzing 0.9.3b)
circuit board: 23.1838cm x 13.0483cm
breadboards: 1

parts:
  Part1 = Arduino Due (Rev2b)
  R6 = Resistor [tolerance=±5% resistance=330 package=THT]
  R5 = Resistor [tolerance=±5% resistance=330 package=THT]
  R7 = Resistor [tolerance=±5% resistance=330 package=THT]
  R3 = Resistor [tolerance=±5% resistance=330 package=THT]
  R1 = Resistor [tolerance=±5% resistance=330 package=THT]
  R2 = Resistor [tolerance=±5% resistance=330 package=THT]
  R8 = Resistor [tolerance=±5% resistance=330 package=THT]
  R10 = Resistor [tolerance=±5% resistance=330 package=THT]
  R9 = Resistor [tolerance=±5% resistance=330 package=THT]
  R11 = Resistor [tolerance=±5% resistance=330 package=THT]
  R12 = Resistor [tolerance=±5% resistance=330 package=THT]
  R20 = Resistor [tolerance=±5% resistance=330 package=THT]
  R14 = Resistor [tolerance=±5% resistance=330 package=THT]
  R15 = Resistor [tolerance=±5% resistance=330 package=THT]
  R16 = Resistor [tolerance=±5% resistance=330 package=THT]
  R17 = Resistor [tolerance=±5% resistance=330 package=THT]
  R18 = Resistor [tolerance=±5% resistance=330 package=THT]
  R19 = Resistor [tolerance=±5% resistance=330 package=THT]
  R10_2 = Resistor [tolerance=±5% resistance=330 package=THT]
  Part1_2 = Arduino Nano (Rev3.0)
  Part3 = Arduino Nano (Rev3.0)
  Part4 = Arduino Nano (Rev3.0)
  Part5 = Arduino Nano (Rev3.0)
  Part6 = Arduino Nano (Rev3.0)
  Part7 = Arduino Nano (Rev3.0)
  Part8 = Arduino Nano (Rev3.0)
  Part9 = Arduino Nano (Rev3.0)
  Part10 = Arduino Nano (Rev3.0)
  Part11 = Arduino Nano (Rev3.0)
  R11_2 = Resistor [tolerance=±5% resistance=330 package=THT]
  Q23 = NPN-Transistor [package="TO92 [THT]"]
  Q14 = NPN-Transistor [package="TO92 [THT]"]
  Q16 = NPN-Transistor [package="TO92 [THT]"]
  Q22 = NPN-Transistor [package="TO92 [THT]"]
  Q20 = NPN-Transistor [package="TO92 [THT]"]
  Q11 = NPN-Transistor [package="TO92 [THT]"]
  Q21 = NPN-Transistor [package="TO92 [THT]"]
  Q15 = NPN-Transistor [package="TO92 [THT]"]
  Q17 = NPN-Transistor [package="TO92 [THT]"]
  Q19 = NPN-Transistor [package="TO92 [THT]"]
  Q10 = NPN-Transistor [package="TO92 [THT]"]
  Q7 = NPN-Transistor [package="TO92 [THT]"]
  Q3 = NPN-Transistor [package="TO92 [THT]"]
  Q9 = NPN-Transistor [package="TO92 [THT]"]
  Q1 = NPN-Transistor [package="TO92 [THT]"]
  Q8 = NPN-Transistor [package="TO92 [THT]"]
  Q4 = NPN-Transistor [package="TO92 [THT]"]
  Q5 = NPN-Transistor [package="TO92 [THT]"]
  Q2 = NPN-Transistor [package="TO92 [THT]"]
  Q6 = NPN-Transistor [package="TO92 [THT]"]
  J2 = female pin header, 8 pins [form="♀ (female)"]
  J3 = female pin header, 2 pins [form="♀ (female)"]
  J4 = female pin header, 6 pins [form="♀ (female)"]
  U1 = ESP-12F [part_number=ESP-12F]
  SW1 = DIP Switch 8 Position [package=dipswitch-08]
  J5 = female pin header, 8 pins [form="♀ (female)"]
  J6 = female pin header, 8 pins [form="♀ (female)"]
  J7 = female pin header, 8 pins [form="♀ (female)"]
  J8 = female pin header, 8 pins [form="♀ (female)"]
  J9 = female pin header, 8 pins [form="♀ (female)"]
  J10 = female pin header, 8 pins [form="♀ (female)"]
  J11 = female pin header, 8 pins [form="♀ (female)"]
  J12 = female pin header, 8 pins [form="♀ (female)"]
  J13 = female pin header, 8 pins [form="♀ (female)"]
  J14 = female pin header, 2 pins [form="♀ (female)"]
  J15 = female pin header, 2 pins [form="♀ (female)"]
  J16 = female pin header, 2 pins [form="♀ (female)"]
  J17 = female pin header, 2 pins [form="♀ (female)"]
  J18 = female pin header, 2 pins [form="♀ (female)"]
  J19 = female pin header, 2 pins [form="♀ (female)"]
  J20 = female pin header, 2 pins [form="♀ (female)"]
  J21 = female pin header, 2 pins [form="♀ (female)"]
  J22 = female pin header, 2 pins [form="♀ (female)"]
  S1 = Momentary Switch [package=ksa_sealed_tac_switch]
  J1 = female pin header, 4 pins [form="♀ (female)"]
  J23 = female pin header, 4 pins [form="♀ (female)"]
  M1 = RioRand LM2596
  J24 = female pin header, 2 pins [form="♀ (female)"]
  X1 = USB Connectors [package=usb-a-s-nosilk-female]

nets:
  N1: Part1.D14/TX3, Q11.C, Q21.C, Q15.C, Q17.C, Q19.C, Q10.C, Q7.C, Q9.C, Q8.C, Q5.C
  N2: Part1.D15/RX3, Q23.E, Q14.E, Q16.E, Q22.E, Q20.E, Q3.E, Q1.E, Q4.E, Q2.E, Q6.E
  N3: Part1.D16/TX2, J23.pin3
  N4: Part1.D17/RX2, J23.pin2
  N5: Part1.D18/TX1, SW1.5
  N6: Part1.D19/RX1, SW1.6
  N7: Part1.IOREF, U1.pad3, U1.pad8
  N8: Part1.MASTER-RESET, SW1.14
  N9: Part1.5V, J4.pin2
  GND: Part1.GND, J4.pin1, U1.pad15, SW1.3, SW1.4, S1.3, J1.pin3, J23.pin1, M1.Pin_4, X1.GND
  N10: Part1.VIN, J1.pin4
  N11: Part1.D10_PWM/SS0, J4.pin6
  N12: Part1.D11_PWM, J4.pin5
  N13: Part1.D12_PWM, J4.pin4
  N14: Part1.D13_PWM, J4.pin3
  N15: Part1.D0/RX, SW1.7
  N16: Part1.D1/TX, SW1.8
  N17: Part1.D28, R1.Pin_1
  N18: Part1.D29, R11_2.Pin_0
  N19: Part1.D30, R2.Pin_1
  N20: Part1.D31, R7.Pin_0
  N21: Part1.D32, R3.Pin_1
  N22: Part1.D33, R5.Pin_0
  N23: Part1.D34, R14.Pin_1
  N24: Part1.D35, R6.Pin_0
  N25: Part1.D36, R15.Pin_1
  N26: Part1.D37, R8.Pin_0
  N27: Part1.D38, R16.Pin_1
  N28: Part1.D39, R9.Pin_0
  N29: Part1.D40, R17.Pin_1
  N30: Part1.D41, R10.Pin_0
  N31: Part1.D42, R18.Pin_1
  N32: Part1.D43, R11.Pin_0
  N33: Part1.D44, R19.Pin_1
  N34: Part1.D45, R12.Pin_0
  N35: Part1.D46, R10_2.Pin_1
  N36: Part1.D47, R20.Pin_0
  N37: R6.Pin_1, Q8.B
  N38: R5.Pin_1, Q4.B
  N39: R7.Pin_1, Q5.B
  N40: R3.Pin_0, Q14.B
  N41: R1.Pin_0, Q23.B
  N42: R2.Pin_0, Q11.B
  N43: R8.Pin_1, Q1.B
  N44: R10.Pin_1, Q3.B
  N45: R9.Pin_1, Q9.B
  N46: R11.Pin_1, Q7.B
  N47: R12.Pin_1, Q6.B
  N48: R20.Pin_1, Q10.B
  N49: R14.Pin_0, Q21.B
  N50: R15.Pin_0, Q16.B
  N51: R16.Pin_0, Q15.B
  N52: R17.Pin_0, Q22.B
  N53: R18.Pin_0, Q17.B
  N54: R19.Pin_0, Q20.B
  N55: R10_2.Pin_0, Q19.B
  GND_2: Part1_2.GND, Part3.GND, Part4.GND, Part5.GND, Part6.GND, Part7.GND, Part8.GND, Part9.GND, Part10.GND, Part11.GND, J3.pin2, J14.pin2, J15.pin2, J16.pin2, J17.pin2, J18.pin2, J19.pin2, J20.pin2, J21.pin2, J22.pin2, J1.pin1
  N56: Part1_2.D2, Q11.E
  N57: Part1_2.D3, Q23.C
  N58: Part1_2.D4, J2.pin8
  N59: Part1_2.D5, J2.pin7
  N60: Part1_2.D6, J2.pin6
  N61: Part1_2.D7, J2.pin5
  N62: Part1_2.D8, J2.pin4
  N63: Part1_2.D9, J2.pin3
  N64: Part1_2.D10, J2.pin2
  N65: Part1_2.D11/MOSI, J2.pin1
  VIN: Part1_2.VIN, Part3.VIN, Part4.VIN, Part5.VIN, Part6.VIN, Part7.VIN, Part8.VIN, Part9.VIN, Part10.VIN, Part11.VIN, J1.pin2
  N66: Part1_2.5V, J3.pin1
  N67: Part3.D2, Q21.E
  N68: Part3.D3, Q14.C
  N69: Part3.D4, J5.pin8
  N70: Part3.D5, J5.pin7
  N71: Part3.D6, J5.pin6
  N72: Part3.D7, J5.pin5
  N73: Part3.D8, J5.pin4
  N74: Part3.D9, J5.pin3
  N75: Part3.D10, J5.pin2
  N76: Part3.D11/MOSI, J5.pin1
  N77: Part3.5V, J14.pin1
  N78: Part4.D2, Q15.E
  N79: Part4.D3, Q16.C
  N80: Part4.D4, J6.pin8
  N81: Part4.D5, J6.pin7
  N82: Part4.D6, J6.pin6
  N83: Part4.D7, J6.pin5
  N84: Part4.D8, J6.pin4
  N85: Part4.D9, J6.pin3
  N86: Part4.D10, J6.pin2
  N87: Part4.D11/MOSI, J6.pin1
  N88: Part4.5V, J15.pin1
  N89: Part5.D2, Q17.E
  N90: Part5.D3, Q22.C
  N91: Part5.D4, J7.pin8
  N92: Part5.D5, J7.pin7
  N93: Part5.D6, J7.pin6
  N94: Part5.D7, J7.pin5
  N95: Part5.D8, J7.pin4
  N96: Part5.D9, J7.pin3
  N97: Part5.D10, J7.pin2
  N98: Part5.D11/MOSI, J7.pin1
  N99: Part5.5V, J16.pin1
  N100: Part6.D2, Q19.E
  N101: Part6.D3, Q20.C
  N102: Part6.D4, J8.pin8
  N103: Part6.D5, J8.pin7
  N104: Part6.D6, J8.pin6
  N105: Part6.D7, J8.pin5
  N106: Part6.D8, J8.pin4
  N107: Part6.D9, J8.pin3
  N108: Part6.D10, J8.pin2
  N109: Part6.D11/MOSI, J8.pin1
  N110: Part6.5V, J17.pin1
  N111: Part7.D2, Q10.E
  N112: Part7.D3, Q6.C
  N113: Part7.D4, J9.pin8
  N114: Part7.D5, J9.pin7
  N115: Part7.D6, J9.pin6
  N116: Part7.D7, J9.pin5
  N117: Part7.D8, J9.pin4
  N118: Part7.D9, J9.pin3
  N119: Part7.D10, J9.pin2
  N120: Part7.D11/MOSI, J9.pin1
  N121: Part7.5V, J18.pin1
  N122: Part8.D2, Q9.E
  N123: Part8.D3, Q1.C
  N124: Part8.D4, J11.pin8
  N125: Part8.D5, J11.pin7
  N126: Part8.D6, J11.pin6
  N127: Part8.D7, J11.pin5
  N128: Part8.D8, J11.pin4
  N129: Part8.D9, J11.pin3
  N130: Part8.D10, J11.pin2
  N131: Part8.D11/MOSI, J11.pin1
  N132: Part8.5V, J20.pin1
  N133: Part9.D2, Q8.E
  N134: Part9.D3, Q4.C
  N135: Part9.D4, J12.pin8
  N136: Part9.D5, J12.pin7
  N137: Part9.D6, J12.pin6
  N138: Part9.D7, J12.pin5
  N139: Part9.D8, J12.pin4
  N140: Part9.D9, J12.pin3
  N141: Part9.D10, J12.pin2
  N142: Part9.D11/MOSI, J12.pin1
  N143: Part9.5V, J21.pin1
  N144: Part10.D2, Q5.E
  N145: Part10.D3, Q2.C
  N146: Part10.D4, J13.pin8
  N147: Part10.D5, J13.pin7
  N148: Part10.D6, J13.pin6
  N149: Part10.D7, J13.pin5
  N150: Part10.D8, J13.pin4
  N151: Part10.D9, J13.pin3
  N152: Part10.D10, J13.pin2
  N153: Part10.D11/MOSI, J13.pin1
  N154: Part10.5V, J22.pin1
  N155: Part11.D2, Q7.E
  N156: Part11.D3, Q3.C
  N157: Part11.D4, J10.pin8
  N158: Part11.D5, J10.pin7
  N159: Part11.D6, J10.pin6
  N160: Part11.D7, J10.pin5
  N161: Part11.D8, J10.pin4
  N162: Part11.D9, J10.pin3
  N163: Part11.D10, J10.pin2
  N164: Part11.D11/MOSI, J10.pin1
  N165: Part11.5V, J19.pin1
  N166: R11_2.Pin_1, Q2.B
  N167: U1.pad1, S1.2
  N168: U1.pad18, SW1.13
  N169: U1.pad21, SW1.10, SW1.12
  N170: U1.pad22, SW1.9, SW1.11
  N171: J23.pin4, M1.Pin_3, X1.VBUS
  N172: M1.Pin_1, J24.pin2
  N173: M1.Pin_2, J24.pin1

custom parts:
  ESP-12F: <>The ESP-12F is a processor module, originally produced by AI-Thinker, with built-in WiFI capabilities and based on the ESP8266 MCU produced by Espressif Systems. Links: Product Specification Espressif Systems ESP8266 MCU
