# Fritzing sketch main_board (saved by Fritzing 0.9.3b)
circuit board: 10.2558cm x 5.45925cm
breadboards: 1

parts:
  Gizwits_WiFi_Witty_ESP-12F1 = Gizwits WiFi Witty ESP-12F
  SW3 = DIP Switch 8 Position [package=dipswitch-08]
  S3 = Momentary Switch [package=ksa_sealed_tac_switch]
  Part3 = Arduino Mega 2560 (Rev3)
  U1 = Mini-360 DC-DC Buck converter [package=THT]
  U2 = Mini-360 DC-DC Buck converter [package=THT]
  J2 = female pin header, 2 pins [form="♀ (female)"]
  X2 = USB Connectors [package=usb-a-s-nosilk-female]
  J3 = female pin header, 10 pins [form="♀ (female)"]
  J4 = female pin header, 8 pins [form="♀ (female)"]
  J5 = female pin header, 2 pins [form="♀ (female)"]
  J6 = female pin header, 2 pins [form="♀ (female)"]
  J7 = female pin header, 2 pins [form="♀ (female)"]

nets:
  N1: Gizwits_WiFi_Witty_ESP-12F1.REST, S3.2
  VCC: Gizwits_WiFi_Witty_ESP-12F1.CH_PD, Gizwits_WiFi_Witty_ESP-12F1.VCC, Part3.3V3
  GND: Gizwits_WiFi_Witty_ESP-12F1.GND, SW3.13, SW3.14, S3.3, Part3.GND, U1.IN-, U1.OUT-, U2.IN-, U2.OUT-, J2.pin1, X2.GND, J5.pin1, J6.pin1, J7.pin1
  N2: Gizwits_WiFi_Witty_ESP-12F1.GPIO0, SW3.4
  N3: Gizwits_WiFi_Witty_ESP-12F1.RXD, SW3.5, SW3.7
  N4: Gizwits_WiFi_Witty_ESP-12F1.TXD, SW3.6, SW3.8
  N5: SW3.3, Part3.RESET
  N6: SW3.9, Part3.D1_TX0
  N7: SW3.10, Part3.D0_RX0
  N8: SW3.11, Part3.D19/RX1
  N9: SW3.12, Part3.D18/TX1
  N10: Part3.VIN, U1.IN+, U2.IN+, J2.pin2
  N11: Part3.D32, J3.pin1
  N12: Part3.D34, J3.pin2
  N13: Part3.D35, J4.pin1
  N14: Part3.D36, J3.pin3
  N15: Part3.D37, J4.pin2
  N16: Part3.D38, J3.pin4
  N17: Part3.D39, J4.pin3
  N18: Part3.D40, J3.pin5
  N19: Part3.D41, J4.pin4
  N20: Part3.D42, J3.pin6
  N21: Part3.D43, J4.pin5
  N22: Part3.D44, J3.pin7
  N23: Part3.D45, J4.pin6
  N24: Part3.D46, J3.pin8
  N25: Part3.D47, J4.pin7
  N26: Part3.D48, J3.pin9
  N27: Part3.D49, J4.pin8
  N28: Part3.D50, J3.pin10
  N29: U1.OUT+, J6.pin2, J7.pin2
  N30: U2.OUT+, X2.VBUS, J5.pin2

custom parts:
  Mini-360 DC-DC Buck converter: Mini-360 DC-DC Buck converter. Tiny buck step down voltage converter, input voltage 4.75 to 23V output 1 to 17V adjustable. Available from ebay and the like.
